// Logisim project BerkemNohutcuFinal.circ as structural Verilog: 5 circuits, main circuit ALU
module ALU (
  input  [7:0] a,
  input  [7:0] b,
  input  [2:0] opcode,
  output [7:0] out_4,
  output iszero
);

  wire [0:0] comparator_1_lt;
  wire [7:0] adder_1_out, and_1_out, nor_1_out, or_1_out, subtractor_1_out, xnor_1_out, xor_1_out;

  assign or_1_out = a | b;  // OR_Gate or_1, 8 bits wide
  Adder adder_1 (.a(a), .b(b), .out(adder_1_out));  // open: cin, cout
  Subtractor subtractor_1 (.a(a), .b(b), .out(subtractor_1_out));  // open: bin, bout
  Comparator comparator_1 (.a(a), .b(b), .lt(comparator_1_lt[0]));  // open: gt, eq
  assign xor_1_out = a ^ b;  // XOR_Gate xor_1, 8 bits wide
  assign xnor_1_out = ~(a ^ b);  // XNOR_Gate xnor_1, 8 bits wide
  assign nor_1_out = ~(a | b);  // NOR_Gate nor_1, 8 bits wide
  assign and_1_out = a & b;  // AND_Gate and_1, 8 bits wide
  Multiplexer #(.select(3), .width(8)) multiplexer_1 (
    .in0(and_1_out), .in1(or_1_out), .in2(adder_1_out), .in3(subtractor_1_out),
    .in4({{7{1'b0}}, comparator_1_lt[0]}), .in5(xor_1_out), .in6(xnor_1_out), .in7(nor_1_out), .out(out_4),
    .sel(opcode));  // open: en
  nor nor_2 (iszero, out_4[0], out_4[1], out_4[2], out_4[3], out_4[4], out_4[5], out_4[6], out_4[7]);
endmodule

module main (
);

  wire alu_1_iszero, and_1_out, CLK, controller_1_alusrc, controller_1_branch, controller_1_jump,
       controller_1_memtoread, controller_1_memtoreg, controller_1_memtowrite, controller_1_regdst,
       controller_1_regwrite;
  wire [1:0] controller_1_alu_1;
  wire [2:0] alu_controller_1_alu_control, multiplexer_1_out;
  wire [3:0] rom_1_data_2;
  wire [7:0] adder_1_out, adder_2_out, alu_1_out_4, multiplexer_2_out, multiplexer_3_out, multiplexer_4_out,
       multiplexer_5_out, ram_1_data, regfield_1_rd1, regfield_1_rd2, register_1_q;
  wire [13:0] rom_1_data;

  Register register_1 (.D(multiplexer_4_out), .Q(register_1_q), .clk(CLK));  // open: en, clr
  Adder adder_1 (.a(register_1_q), .b(8'h1), .out(adder_1_out));  // open: cin, cout
  Clock clock_1 (.out(CLK));
  Controller controller_1 (
    .in_1(rom_1_data_2), .RegdST(controller_1_regdst), .jump(controller_1_jump),
    .branch(controller_1_branch), .memtoread(controller_1_memtoread), .memtoreg(controller_1_memtoreg),
    .alu_1(controller_1_alu_1[0]), .alu_2(controller_1_alu_1[1]), .memtowrite(controller_1_memtowrite),
    .AluSRC(controller_1_alusrc), .RegWrite(controller_1_regwrite));
  ROM #(.dataWidth(18)) rom_1 (.addr(register_1_q), .data({rom_1_data_2, rom_1_data}));  // open: sel
  Multiplexer #(.width(3), .enable("false")) multiplexer_1 (
    .in0(rom_1_data[10:8]), .in1(rom_1_data[7:5]), .out(multiplexer_1_out), .sel(controller_1_regdst));
  regfield regfield_1 (
    .A1(rom_1_data[13:11]), .A2(rom_1_data[10:8]), .A3(multiplexer_1_out), .WE3(controller_1_regwrite),
    .WD3(multiplexer_5_out), .CLK(CLK), .RD1(regfield_1_rd1), .RD2(regfield_1_rd2));  // open: Reset
  Multiplexer #(.width(8), .enable("false")) multiplexer_2 (
    .in0(regfield_1_rd2), .in1(rom_1_data[7:0]), .out(multiplexer_2_out), .sel(controller_1_alusrc));
  ALU_Controller alu_controller_1 (
    .ALUOP(controller_1_alu_1), .instr(rom_1_data[2:0]), .Alu_Control(alu_controller_1_alu_control));
  ALU alu_1 (
    .a(regfield_1_rd1), .b(multiplexer_2_out), .opcode(alu_controller_1_alu_control), .out_4(alu_1_out_4),
    .iszero(alu_1_iszero));
  and and_1 (and_1_out, controller_1_branch, alu_1_iszero);
  Adder adder_2 (.a(adder_1_out), .b(rom_1_data[7:0]), .out(adder_2_out));  // open: cin, cout
  RAM ram_1 (
    .addr(alu_1_out_4), .data(ram_1_data), .sel(controller_1_memtowrite), .clk(CLK),
    .ld(controller_1_memtoread));  // open: clr
  Multiplexer #(.width(8), .enable("false")) multiplexer_3 (
    .in0(adder_1_out), .in1(adder_2_out), .out(multiplexer_3_out), .sel(and_1_out));
  Multiplexer #(.width(8), .enable("false")) multiplexer_4 (
    .in0(multiplexer_3_out), .in1(rom_1_data[7:0]), .out(multiplexer_4_out), .sel(controller_1_jump));
  Multiplexer #(.width(8), .enable("false")) multiplexer_5 (
    .in0(alu_1_out_4), .in1(ram_1_data), .out(multiplexer_5_out), .sel(controller_1_memtoreg));

  // Notes on the sheet:
  //   contents of rom_1 (hex, n*v repeats v):
  //   2010e 2021a 2301 1542 1583 15c5 2c800 2d004 2d808 2e00c 2e810 2f014 2f818
endmodule

module regfield (
  input  CLK,
  input  Reset,
  input  [2:0] A1,
  input  [2:0] A2,
  input  [2:0] A3,
  input  WE3,
  input  [7:0] WD3,
  output [7:0] RD1,
  output [7:0] RD2
);

  wire demultiplexer_1_out0, demultiplexer_1_out1, demultiplexer_1_out2, demultiplexer_1_out3,
       demultiplexer_1_out4, demultiplexer_1_out5, demultiplexer_1_out6, demultiplexer_1_out7;
  wire [7:0] r0_q, r1_q, r2_q, r3_q, r4_q, r5_q, r6_q, r7_q;

  Demultiplexer #(.select(3), .enable("false")) demultiplexer_1 (
    .out0(demultiplexer_1_out0), .out1(demultiplexer_1_out1), .out2(demultiplexer_1_out2),
    .out3(demultiplexer_1_out3), .out4(demultiplexer_1_out4), .out5(demultiplexer_1_out5),
    .out6(demultiplexer_1_out6), .out7(demultiplexer_1_out7), .in(WE3), .sel(A3));
  Register r0 (.D(WD3), .en(demultiplexer_1_out0), .Q(r0_q), .clk(CLK), .clr(Reset));
  Register r4 (.D(WD3), .en(demultiplexer_1_out4), .Q(r4_q), .clk(CLK), .clr(Reset));
  Register r1 (.D(WD3), .en(demultiplexer_1_out1), .Q(r1_q), .clk(CLK), .clr(Reset));
  Register r5 (.D(WD3), .en(demultiplexer_1_out5), .Q(r5_q), .clk(CLK), .clr(Reset));
  Register r2 (.D(WD3), .en(demultiplexer_1_out2), .Q(r2_q), .clk(CLK), .clr(Reset));
  Register r6 (.D(WD3), .en(demultiplexer_1_out6), .Q(r6_q), .clk(CLK), .clr(Reset));
  Register r3 (.D(WD3), .en(demultiplexer_1_out3), .Q(r3_q), .clk(CLK), .clr(Reset));
  Register r7 (.D(WD3), .en(demultiplexer_1_out7), .Q(r7_q), .clk(CLK), .clr(Reset));
  Multiplexer #(.select(3), .width(8), .enable("false")) multiplexer_1 (
    .in0(r0_q), .in1(r1_q), .in2(r2_q), .in3(r3_q), .in4(r4_q), .in5(r5_q), .in6(r6_q), .in7(r7_q),
    .out(RD1), .sel(A1));
  Multiplexer #(.select(3), .width(8), .enable("false")) multiplexer_2 (
    .in0(r0_q), .in1(r1_q), .in2(r2_q), .in3(r3_q), .in4(r4_q), .in5(r5_q), .in6(r6_q), .in7(r7_q),
    .out(RD2), .sel(A2));
endmodule

module ALU_Controller (
  input  [1:0] ALUOP,
  input  [2:0] instr,
  output [2:0] Alu_Control
);

  wire and_2_out, not_1_out;

  not not_1 (not_1_out, ALUOP[1]);
  and and_1 (Alu_Control[2], ALUOP[1], instr[2]);
  or or_1 (Alu_Control[1], not_1_out, instr[1]);
  and and_2 (and_2_out, instr[0], ALUOP[1]);
  or or_2 (Alu_Control[0], ALUOP[0], and_2_out);
endmodule

module Controller (
  input  [3:0] in_1,
  output RegdST,
  output jump,
  output branch,
  output memtoread,
  output memtoreg,
  output alu_1,
  output alu_2,
  output memtowrite,
  output AluSRC,
  output RegWrite
);

  wire decoder_1_out8;

  Decoder #(.select(4), .enable("false")) decoder_1 (
    .out0(alu_2), .out2(jump), .out3(memtoread), .out4(alu_1), .out8(decoder_1_out8), .out11(memtowrite),
    .sel(in_1));  // open: out1, out5, out6, out7, out9, out10, out12, out13, out14, out15
  or or_1 (AluSRC, memtowrite, decoder_1_out8, memtoread);
  or or_2 (RegWrite, alu_2, memtoread, decoder_1_out8);

  assign branch = alu_1;
  assign memtoreg = memtoread;
  assign RegdST = alu_2;
endmodule
